// Logisim project FullAdderV1.circ as structural Verilog: 1 circuit, main circuit main
module main (
  input  in_1,
  input  in_2,
  output out_3,
  output out_4
);

  wire not_1_out, undriven_2;
  wire [1:0] undriven;

  not not_1 (not_1_out, in_1);
  Multiplexer #(.select(2)) multiplexer_1 (
    .in0(in_1), .in1(not_1_out), .in2(not_1_out), .in3(in_1), .out(out_3), .sel(undriven), .en(undriven_2));
  Multiplexer #(.select(2)) multiplexer_2 (
    .in0(1'b0), .in1(in_2), .in2(in_2), .in3(1'b1), .out(out_4), .sel(undriven), .en(undriven_2));
endmodule
