// Logisim project Contador0a99.circ as structural Verilog: 1 circuit, main circuit main
module main (
  input  in_1,
  input  in_2,
  input  in_3,
  input  in_4,
  input  in_5,
  input  in_6,
  input  in_7,
  input  in_8
);

  wire and_1_out, and_2_out;

  J_K_Flip_Flop j_k_ff_1 (.J(in_5), .clk(1'b1), .K(in_5), .Q(in_1), .en(and_1_out));  // open: Qn, preset, reset
  J_K_Flip_Flop j_k_ff_2 (.J(in_5), .clk(and_1_out), .K(in_5), .Q(in_5), .en(and_2_out));  // open: Qn, preset, reset
  J_K_Flip_Flop j_k_ff_3 (.J(in_5), .clk(in_1), .K(in_5), .Q(in_2), .en(and_1_out));  // open: Qn, preset, reset
  J_K_Flip_Flop j_k_ff_4 (.J(in_5), .clk(in_5), .K(in_5), .Q(in_5), .en(and_2_out));  // open: Qn, preset, reset
  J_K_Flip_Flop j_k_ff_5 (.J(in_5), .clk(in_2), .K(in_5), .Q(in_3), .en(and_1_out));  // open: Qn, preset, reset
  and and_1 (and_1_out, in_2, in_4);
  J_K_Flip_Flop j_k_ff_6 (.J(in_5), .clk(in_5), .K(in_5), .Q(in_5));  // open: Qn, preset, en, reset
  and and_2 (and_2_out, in_5, in_5);
  J_K_Flip_Flop j_k_ff_7 (.J(in_5), .clk(in_3), .K(in_5), .Q(in_4), .en(and_1_out));  // open: Qn, preset, reset
  J_K_Flip_Flop j_k_ff_8 (.J(in_5), .clk(in_5), .K(in_5), .Q(in_5), .en(and_2_out));  // open: Qn, preset, reset
  _7_Segment_Display u_7_segment_display_1 (.e(in_5), .d(in_5), .c(in_5), .dp(in_5));  // open: g, f, a, b
  _7_Segment_Display u_7_segment_display_2 (.g(in_1), .f(in_2), .a(in_3), .b(in_4));  // open: e, d, c, dp

  assign in_6 = in_5;
  assign in_7 = in_5;
  assign in_8 = in_5;
endmodule
